# Fritzing sketch 7seg_4dig (saved by Fritzing 0.9.3b)
breadboards: 1

parts:
  Part1 = Arduino Uno (Rev3)
  R1 = Resistor [tolerance=±5% resistance=220 package=THT]
  R2 = Resistor [tolerance=±5% resistance=220 package=THT]
  R3 = Resistor [tolerance=±5% resistance=220 package=THT]
  R4 = Resistor [tolerance=±5% resistance=220 package=THT]
  7_Segment_4_Digit_Display1 = 7-SEGMENT-4DIGIT common anode [part_number="5461BS - 5462BS" package=7-segment-4digit-anode]

nets:
  N1: Part1.D8, 7_Segment_4_Digit_Display1.pin_4
  N2: Part1.D9_PWM, 7_Segment_4_Digit_Display1.pin_2
  N3: Part1.D10_PWM/SS, 7_Segment_4_Digit_Display1.pin_1
  N4: Part1.D11_PWM/MOSI, 7_Segment_4_Digit_Display1.pin_10
  N5: Part1.D12/MISO, 7_Segment_4_Digit_Display1.pin_5
  N6: Part1.D13/SCK, 7_Segment_4_Digit_Display1.pin_3
  N7: Part1.D2, R4.Pin_1
  N8: Part1.D3_PWM, R3.Pin_1
  N9: Part1.D4, R2.Pin_1
  N10: Part1.D5_PWM, R1.Pin_1
  N11: Part1.D6_PWM, 7_Segment_4_Digit_Display1.pin_11
  N12: Part1.D7, 7_Segment_4_Digit_Display1.pin_7
  N13: R1.Pin_0, 7_Segment_4_Digit_Display1.pin_6
  N14: R2.Pin_0, 7_Segment_4_Digit_Display1.pin_8
  N15: R3.Pin_0, 7_Segment_4_Digit_Display1.pin_9
  N16: R4.Pin_0, 7_Segment_4_Digit_Display1.pin_12

custom parts:
  7-SEGMENT-4DIGIT common anode: A 7 Segment 4 Digit common anode display, with decimal points
