# Fritzing sketch 7seg_display (saved by Fritzing 0.9.3b)
circuit board: 8.46667cm x 5.64444cm
breadboards: 1

parts:
  Arduino_UNO = Arduino Uno (Rev3)
  7_Segment1 = 7 Segment Display
  R1 = Resistor [tolerance=±5% resistance=220 package=THT]

nets:
  N1: Arduino_UNO.D8, Arduino_UNO.D9_PWM, Arduino_UNO.D2, Arduino_UNO.D5_PWM, Arduino_UNO.D6_PWM, Arduino_UNO.D7, 7_Segment1.Segment_G, 7_Segment1.Segment_F, 7_Segment1.Segment_E, 7_Segment1.Segment_D, 7_Segment1.Segment_DP, 7_Segment1.Segment_A
  N2: Arduino_UNO.D3_PWM, Arduino_UNO.D4, 7_Segment1.Segment_C, 7_Segment1.Segment_B
  N3: Arduino_UNO.3V3, R1.Pin_1
  N4: 7_Segment1.common_anode, R1.Pin_0

// code stored in the sketch: Untitled2.ino
#include "SevSeg.h"
SevSeg sevseg; 

void setup(){
  byte numDigits = 1;
  byte digitPins[] = {};
  byte segmentPins[] = {6, 5, 2, 3, 4, 7, 8, 9};
  bool resistorsOnSegments = true;
  byte hardwareConfig = COMMON_ANODE;
  
  sevseg.begin(hardwareConfig, numDigits, digitPins, segmentPins, resistorsOnSegments);
  sevseg.setBrightness(90);
}

void loop(){
  for(int i = 0; i < 10; i++){
    sevseg.setNumber(i, i%2);
    delay(200);
    sevseg.refreshDisplay(); 
  }
}
