# Fritzing sketch WebServer (saved by Fritzing 0.9.3b)
breadboards: 3

parts:
  Componente1 = Arduino Uno (Rev3)
  LED1 = LED - 5mm [color="Red (633nm)" package="5 mm [THT]"]
  LED2 = LED - 5mm [color="Yellow (595nm)" package="5 mm [THT]"]
  LED3 = LED - 5mm [color="Green (555nm)" package="5 mm [THT]"]
  U1 = ESP-12F (ESP8266 WiFi Module) [part_number=ESP8266]
  R2 = Trimmer Potentiometer [maximum_resistance=10kΩ package=THT]
  R3 = Resistor [tolerance=±5% resistance=220 package=THT]
  R4 = Resistor [tolerance=±5% resistance=220 package=THT]
  S1 = Pushbutton [package="[THT]"]
  R1 = Resistor [tolerance=±5% resistance=220 package=THT]

nets (from the schematic view):
  N1: Componente1.D0/RX, U1.RXD0
  N2: Componente1.D1/TX, U1.TXD0
  GND: Componente1.RESET, Componente1.GND, LED1.cathode, LED2.cathode, LED3.cathode, U1.GND, R2.leg2, S1.Pin_3, S1.Pin_4, R1.Pin_0
  N3: LED1.anode, U1.GPIO5
  N4: LED2.anode, U1.GPIO13
  N5: LED3.anode, U1.GPIO4
  N6: U1.GPIO0, R2.wiper
  N7: U1.EN, R4.Pin_0
  N8: U1.GPIO15, R1.Pin_1
  N9: U1.RST, S1.Pin_1, S1.Pin_2
  N10: R2.leg1, R3.Pin_1
  N11: R3.Pin_0, R4.Pin_1

custom parts:
  ESP-12F (ESP8266 WiFi Module): WiFi Module based on the ESP8266 with onboard PCB antenna and UART communications
